# Fritzing sketch mars_rover_4wd (saved by Fritzing 0.9.3b)

parts:
  Raspberry_Pi_Zero1 = Raspberry Pi Zero
  U2 = L9110 H-bridge module [part_number="L9110 H-bridge"]
  M3 = DC Motor
  M5 = DC Motor  # not connected
  M6 = DC Motor
  M7 = DC Motor
  M8 = DC Motor
  U3 = L9110 H-bridge module [part_number="L9110 H-bridge"]
  U4 = L9110 H-bridge module [part_number="L9110 H-bridge"]

nets:
  N1: Raspberry_Pi_Zero1.GPIO4, U4.B-IA
  N2: Raspberry_Pi_Zero1.GPIO17, U4.B-IB
  N3: Raspberry_Pi_Zero1.GPIO27, U4.A-IA
  N4: Raspberry_Pi_Zero1.GPIO22, U4.A-IB
  N5: Raspberry_Pi_Zero1.GPIO5, U2.B-IA
  N6: Raspberry_Pi_Zero1.GPIO6, U2.B-IB
  N7: Raspberry_Pi_Zero1.GPIO13, U2.A-IA
  N8: Raspberry_Pi_Zero1.GPIO26, U2.A-IB
  N9: Raspberry_Pi_Zero1.GPIO25, U3.A-IB
  N10: Raspberry_Pi_Zero1.GPIO24, U3.A-IA
  N11: Raspberry_Pi_Zero1.GPIO23, U3.B-IB
  N12: Raspberry_Pi_Zero1.GPIO18, U3.B-IA
  N13: M3.pin_1, U4.MOTOR_B-B
  N14: M3.pin_2, U4.MOTOR_B-A
  N15: M6.pin_1, U4.MOTOR_A-B
  N16: M6.pin_2, U4.MOTOR_A-A
  N17: M7.pin_1, U3.MOTOR_A-B
  N18: M7.pin_2, U3.MOTOR_A-A
  N19: M8.pin_1, U3.MOTOR_B-B
  N20: M8.pin_2, U3.MOTOR_B-A
